# Fritzing sketch PJONEthernetTunneler (saved by Fritzing 0.9.3b)

parts:
  Part1 = Arduino Uno (Rev3) - ICSP
  Part2 = Arduino Ethernet Shield (Rev3)
  Part3 = Arduino Uno (Rev3) - ICSP
  Part4 = Arduino Uno (Rev3) - ICSP  # not connected
  Part5 = Arduino Uno (Rev3) - ICSP  # not connected
  Part6 = Arduino Ethernet Shield (Rev3)

nets:
  GND: Part1.GND, Part6.GND
  N1: Part1.D12/MISO, Part6.D7
  VIN: Part1.VIN, Part6.VIN
  N2: Part2.D7, Part3.D12/MISO
  GND_2: Part2.GND, Part3.GND
  VIN_2: Part2.VIN, Part3.VIN

notes:
  PJONEthernetTunnel role 1 (id 44) on Uno+Ethernet
  PJONEthernetTunnel role 0 (id 45) on Uno+Ethernet
  PJONDevicel 1 (id 44)
  PJONDevice 2 (id 45)
  Bidirectional tunneling of  PJON traffic through Ethernet
